// Logisim project RtypeSub.circ as structural Verilog: 1 circuit, main circuit main
module main (
  input  [15:0] InputA,
  input  [15:0] InputB,
  input  DataControl,
  input  CLR,
  input  RegWrite,
  input  RegClear,
  input  outputAddressControl,
  input  Binvert,
  output Cout,
  output [15:0] Data1,
  output [15:0] Data2,
  output [15:0] OutputValue,
  output [3:0] RegisterAddress
);

  wire CLK_out, multiplexer_3_out, not_1_out, RegClock_out;
  wire [3:0] register_1_p1, rom_1_data;
  wire [15:0] adder_1_out, alu16bit_1_p6, PC_q, register_1_p3, register_1_p6;
  wire [15:8] register_1_p2;

  Clock CLK (.out(CLK_out));
  Register #(.width(16)) PC (.D(adder_1_out), .Q(PC_q), .clk(CLK_out), .clr(CLR));  // open: en
  Clock RegClock (.out(RegClock_out));
  // register register_1: pin names not known; wires that end beside it: register_1_p1, register_1_p2[11:8], register_1_p3, register_1_p1, register_1_p2[11:8], register_1_p6, DataControl, RegClock_out, RegWrite, Data1, Data2, RegClear
  Adder #(.width(16)) adder_1 (.a(16'h1), .b(PC_q), .out(adder_1_out));  // open: cin, cout
  Multiplexer #(.width(4), .enable("false")) multiplexer_1 (
    .in0(rom_1_data), .in1(RegisterAddress), .out(register_1_p1), .sel(outputAddressControl));
  ROM #(.addrWidth(16), .dataWidth(16)) rom_1 (
    .addr(PC_q), .data({register_1_p2, rom_1_data, RegisterAddress}));  // open: sel
  not not_1 (not_1_out, register_1_p2[14]);
  Multiplexer #(.width(16), .enable("false")) multiplexer_2 (
    .in0(InputB), .out(register_1_p6), .sel(outputAddressControl));  // open: in1
  Multiplexer #(.enable("false")) multiplexer_3 (
    .in0(register_1_p2[14]), .in1(not_1_out), .out(multiplexer_3_out), .sel(Binvert));
  Multiplexer #(.width(16), .enable("false")) multiplexer_4 (
    .in0(InputA), .in1(OutputValue), .out(register_1_p3), .sel(outputAddressControl));
  // ALU16bit alu16bit_1: pin names not known; wires that end beside it: Data1, Data2, register_1_p2[13:12], multiplexer_3_out, multiplexer_3_out, alu16bit_1_p6, Cout
  RAM #(.addrWidth(4), .dataWidth(16), .bus("separate")) ram_1 (
    .addr(RegisterAddress), .din(alu16bit_1_p6), .data(OutputValue), .clk(outputAddressControl), .clr(CLR));  // open: str, sel, ld

  // Notes on the sheet:
  //   contents of rom_1 (hex, n*v repeats v):
  //   2345 2678
endmodule
